# Fritzing sketch L298N (saved by Fritzing 0.8.7b)

parts:
  元件1 = Arduino Uno (Rev3)
  S1 = H-Bridge with L298N
  M1 = DC Motor
  M2 = DC Motor
  S2 = H-Bridge with L298N
  M3 = DC Motor
  M4 = DC Motor

nets:
  N1: 元件1.D8, S1.IN1
  N2: 元件1.D9_PWM, S1.5V
  N3: 元件1.D10_PWM/SS, S1.IN2
  N4: 元件1.D11_PWM/MOSI, S1.IN3
  N5: 元件1.D12/MISO, S1.IN4
  N6: 元件1.D3_PWM, S2.IN1
  N7: 元件1.D4, S2.IN2
  N8: 元件1.D5_PWM, S2.IN3
  N9: 元件1.D6_PWM, S2.5V
  N10: 元件1.D7, S2.IN4
  N11: S1.M1-01, M1.pin_2
  N12: S1.M1-02, M1.pin_1
  N13: S1.M2-01, M2.pin_2
  N14: S1.M2-02, M2.pin_1
  N15: S2.M1-01, M3.pin_2
  N16: S2.M1-02, M3.pin_1
  N17: S2.M2-01, M4.pin_2
  N18: S2.M2-02, M4.pin_1

custom parts:
  H-Bridge with L298N: h-bridge
