# Fritzing sketch hc-05-serial (saved by Fritzing 0.8.7b)

parts:
  Part1 = Bluetooth HC-05 Macho
  元件1 = Arduino Uno (Rev3) - ICSP

nets:
  N1: Part1.TXD, 元件1.D0/RX
  N2: Part1.RXD, 元件1.D1/TX
  VCC: Part1.VCC, 元件1.5V
  GND: Part1.GND, 元件1.GND
