# Fritzing sketch HC-SR04 (saved by Fritzing 0.8.7b)

parts:
  Bauteil1 = Arduino Uno (Rev3)
  U2 = HC-SR04 [chip_label=IC package="SIP (Single Inline) [THT]"]

nets:
  N1: Bauteil1.D10_PWM/SS, U2.Trig
  N2: Bauteil1.D13/SCK, U2.Echo
  5V: Bauteil1.5V, U2.Vcc
  GND: Bauteil1.GND, U2.GND

custom parts:
  HC-SR04: HC-SR04 ultrasound distance sensor
